# Fritzing sketch DESAIN MONIC (saved by Fritzing 0.9.3b)
breadboards: 1

parts:
  Raspberry_Pi_1 = Raspberry Pi 3 [part_number=RPI-3-V1.2]
  LED1 = LEDs [package=led10mm]
  DHT1 = DHT22 Humidity and Temperature Sensor
  e-radionica_com1 = LM393 LDR breakout [part_number=100027]
  HC-SR04_Sensor_1 = HC-SR04 Ultrasonic Distance Sensor

nets:
  N1: Raspberry_Pi_1.GPIO2, DHT1.DATA
  N2: Raspberry_Pi_1.GPIO17, Raspberry_Pi_1.GPIO18, LED1.A
  N3: Raspberry_Pi_1.GPIO24, HC-SR04_Sensor_1.ECHO
  N4: Raspberry_Pi_1.GPIO23, HC-SR04_Sensor_1.TRIG
  GND: Raspberry_Pi_1.GND, DHT1.GND, e-radionica_com1.GND, HC-SR04_Sensor_1.GND
  N5: Raspberry_Pi_1.GPIO15, e-radionica_com1.DO
  VCC: Raspberry_Pi_1.5V, LED1.C, DHT1.VDD, e-radionica_com1.VCC, HC-SR04_Sensor_1.VCC
